// Logisim project 2b ALU.circ as structural Verilog: 3 circuits, main circuit 2b ALU
module _2b_ALU (
  input  [1:0] A,
  input  [2:0] Op,
  input  Sub,
  input  [1:0] B,
  input  in_5,
  input  in_6,
  output [1:0] Result1,
  output [1:0] out_8,
  output out_9,
  output [1:0] out_10,
  output [3:0] Multiply
);

  wire n1b_alu_1_out_7;

  _1b_ALU u_1b_alu_1 (
    .A(A[0]), .B(B[0]), .Result(Result1[0]), .sub(Sub), .cin(Sub), .in_4(Op), .out_7(n1b_alu_1_out_7));
  _1b_ALU u_1b_alu_2 (
    .A(A[1]), .B(B[1]), .Result(Result1[1]), .sub(Sub), .cin(n1b_alu_1_out_7), .in_4(Op), .out_7(out_9));
  Multiplier multiplier_1 (
    .A0(A[0]), .A1(A[1]), .B0(B[0]), .B1(B[1]), .in_5(in_6), .R0(Multiply[0]), .R1(Multiply[1]),
    .R2(Multiply[2]), .R4(Multiply[3]));
  Multiplexer #(.width(2), .enable("false")) multiplexer_1 (
    .in0(Result1), .in1(Multiply[1:0]), .out(out_8), .sel(in_5));

  assign out_10 = Multiply[1:0];
endmodule

module _1b_ALU (
  input  sub,
  input  cin,
  input  A,
  input  [2:0] in_4,
  input  B,
  output Result,
  output out_7
);

  wire adder_1_out, and_1_out, not_1_out, or_1_out, xor_1_out, xor_2_out;

  xor xor_1 (xor_1_out, B, sub);
  not not_1 (not_1_out, A);
  and and_1 (and_1_out, A, B);
  or or_1 (or_1_out, A, B);
  xor xor_2 (xor_2_out, A, B);
  Adder #(.width(1)) adder_1 (.a(A), .b(xor_1_out), .out(adder_1_out), .cin(cin), .cout(out_7));
  Multiplexer #(.select(3), .enable("false")) multiplexer_1 (
    .in0(not_1_out), .in1(and_1_out), .in2(or_1_out), .in3(xor_2_out), .in4(adder_1_out), .out(Result),
    .sel(in_4));  // open: in5, in6, in7
endmodule

module Multiplier (
  input  A0,
  input  A1,
  input  B0,
  input  B1,
  input  in_5,
  output R0,
  output R1,
  output R2,
  output R4
);

  wire adder_1_cout, and_2_out, and_3_out, and_4_out;

  and and_1 (R0, A0, B0);
  and and_2 (and_2_out, A0, B1);
  and and_3 (and_3_out, A1, B0);
  and and_4 (and_4_out, A1, B1);
  Adder #(.width(1)) adder_1 (.a(and_2_out), .b(and_3_out), .out(R1), .cout(adder_1_cout));  // open: cin
  Adder #(.width(1)) adder_2 (.a(and_4_out), .b(in_5), .out(R2), .cin(adder_1_cout), .cout(R4));
endmodule
